# Fritzing sketch mosfet (saved by Fritzing 0.9.3b)
breadboards: 1

parts:
  Part1 = Arduino Uno (Rev3)
  R1 = Rotary Potentiometer (Small) [maximum_resistance=100kΩ package=THT]
  Q1 = MOSFET-NCHANNEL [package=to220v]
  D1 = Rectifier Diode [part_number=1N4001 package="300 mil [THT]"]
  J1 = Power Jack [package=power_jack_smd]
  M1 = DC Motor

nets:
  N1: Part1.A0, R1.wiper
  N2: Part1.D3_PWM, Q1.G
  N3: Part1.5V, R1.leg1
  N4: Part1.GND, R1.leg2, Q1.S, D1.anode, J1.GNDBREAK
  N5: Q1.D, D1.cathode, M1.pin_1
  N6: J1.GND, M1.pin_2
