# Fritzing sketch switchpushbutton (saved by Fritzing 0.9.4)
breadboards: 1

parts:
  Part1 = Arduino Uno (Rev3)
  R1 = Resistor [tolerance=±5% resistance=10k package=THT]
  S3 = Pushbutton [package="[THT]"]

nets:
  N1: Part1.D2, R1.Pin_0, S3.Pin_1, S3.Pin_2
  N2: Part1.5V, S3.Pin_3, S3.Pin_4
  N3: Part1.GND, R1.Pin_1
